// Digital circuit BoothsMultiplierPart1.dig as structural Verilog
module BoothsMultiplierPart1 (
  input  CLK,
  input  CLR,
  input  [12:0] MULTIPLICAND,
  input  [12:0] MULTIPLIER,
  output DONE,
  output [1:0] OP_DONE,
  output [25:0] RESULT
);

  wire INIT_INPUT, LOAD_INPUT, or_1_out, or_2_out, SHIFT_INPUT;
  wire [12:0] demultiplexer_1_out_0, demultiplexer_1_out_1, demultiplexer_2_out_1, MULTIPLICAND_p7;
  wire [12:1] demultiplexer_2_out_0;
  wire [13:0] ACCUMULATOR_p6, add_1_s, bitextender_1_out, bitextender_2_out, bitextender_3_out,
       MULTIPLICAND_DATA, sub_1_s;

  // ControlUnit controlunit_1: pin names not known; wires that end beside it: CLK, CLR, DONE, INIT_INPUT, LOAD_INPUT, SHIFT_INPUT
  or or_1 (or_1_out, LOAD_INPUT, INIT_INPUT, SHIFT_INPUT);
  // Shifter ACCUMULATOR: pin names not known; wires that end beside it: or_1_out, INIT_INPUT, LOAD_INPUT, SHIFT_INPUT, RESULT[25], ACCUMULATOR_p6[12:0], RESULT[25:13]
  // Probe on RESULT[25:13]
  Demultiplexer #(.Bits(13)) demultiplexer_1 (
    .sel(SHIFT_INPUT), .in(RESULT[25:13]), .out_0(demultiplexer_1_out_0), .out_1(demultiplexer_1_out_1));
  BitExtender #(.inputBits(13), .outputBits(14)) bitextender_1 (.in(demultiplexer_1_out_0), .out(bitextender_1_out));
  Add #(.Bits(14)) add_1 (.a(bitextender_1_out), .b(MULTIPLICAND_DATA), .c_i(1'b0), .s(add_1_s));  // open: c_o
  BitExtender #(.inputBits(13), .outputBits(14)) bitextender_2 (.in(RESULT[25:13]), .out(bitextender_2_out));
  BitExtender #(.inputBits(13), .outputBits(14)) bitextender_3 (.in(RESULT[25:13]), .out(bitextender_3_out));
  Multiplexer #(.Selector_Bits(2), .Bits(14)) multiplexer_1 (
    .sel(OP_DONE), .in_0(bitextender_3_out), .in_1(add_1_s), .in_2(sub_1_s), .in_3(bitextender_2_out),
    .out(ACCUMULATOR_p6));
  or or_2 (or_2_out, INIT_INPUT, SHIFT_INPUT);
  // Shifter MULTIPLIER: pin names not known; wires that end beside it: or_2_out, 1'b0, INIT_INPUT, SHIFT_INPUT, demultiplexer_1_out_1[0], MULTIPLIER, RESULT[12:0]
  Sub #(.Bits(14)) sub_1 (.a(bitextender_1_out), .b(MULTIPLICAND_DATA), .c_i(1'b0), .s(sub_1_s));  // open: c_o
  // Probe on RESULT[12:0]
  Demultiplexer #(.Bits(13)) demultiplexer_2 (
    .sel(SHIFT_INPUT), .in(RESULT[12:0]), .out_0({demultiplexer_2_out_0, OP_DONE[1]}),
    .out_1(demultiplexer_2_out_1));
  // Probe on OP_DONE
  // Shifter MULTIPLICAND: pin names not known; wires that end beside it: INIT_INPUT, 1'b0, INIT_INPUT, 1'b0, 1'b0, MULTIPLICAND, MULTIPLICAND_p7
  D_FF F1 (.D(demultiplexer_2_out_1[0]), .C(SHIFT_INPUT), .Q(OP_DONE[0]));  // open: nQ
  // Probe on MULTIPLICAND_p7
  BitExtender #(.inputBits(13), .outputBits(14)) bitextender_4 (.in(MULTIPLICAND_p7), .out(MULTIPLICAND_DATA));

  // Other names for the same wires on the sheet: ACCUMULATOR_DATA[12:0] = RESULT[25:13]
endmodule
